# Fritzing sketch rpm_computer_side (saved by Fritzing 0.7.12b)
breadboards: 1

parts:
  TRXCOM2 = RJ45-TRXCOM [part_number=TRJ0011BANL]
  J1 = female pin header, 2 pins [form="♀ (female)"]
  J2 = female pin header, 3 pins [form="♀ (female)"]
  J3 = female pin header, 4 pins [form="♀ (female)"]
  Q1 = Basic FET N-Channel [package="TO220 [THT]"]
  R1 = 10k Ω Resistor [package=THT]

nets:
  N1: TRXCOM2.Transmit_TD-, J2.pin1
  N2: TRXCOM2.Receive_RD+, J2.pin3
  N3: TRXCOM2.Receive_CT, J1.pin1
  N4: TRXCOM2.Receive_RD-, J1.pin2
  N5: TRXCOM2.n.c., J3.pin1
  N6: TRXCOM2.CHS_Ground, Q1.gate, R1.Pin_0
  N7: J3.pin2, Q1.drain
  N8: J3.pin3, Q1.source
  N9: J3.pin4, R1.Pin_1

notes:
  Power SW
  Power LED
  ATX PWR
  0V SW PWR
  +5V SW PWR
  LED+
  LED-
  Ground
  Green+
  Green-
  Violet (+5V)
